# Fritzing sketch Sketch (saved by Fritzing 0.9.3b)
breadboards: 4

parts:
  Componente1 = Arduino Mega ADK (Rev3)
  Componente2 = Arduino Ethernet Shield (Rev3)
  RHT1 = Humidity and Temperature Sensor RHT03
  Componente5 = Real Time Clock Module - DS1307 RTC Breakout Board
  LED1 = LED - 5mm [color="Yellow (595nm)" package="5 mm [THT]"]  # not connected
  LED2 = LED - 5mm [color="Red (633nm)" package="5 mm [THT]"]  # not connected
  lm317 = NPN-Transistor [package="TO92 [THT]"]
  Shinyei_PPD42 = female pin header, 5 pins [form="♀ (female)"]
  U1 = LIPO-1000mAh [package=lipo-1000]
  R10 = Resistor [tolerance=±5% resistance=100 package="0402 [SMD]"]
  R11 = Resistor [tolerance=±5% resistance=300 package="0402 [SMD]"]
  C2 = Electrolytic Capacitor [capacitance=1µF package="0605 [SMD, electrolytic]"]
  C1 = Tantalum Capacitor [capacitance=0.1µF package="D 7343 [SMD, tantalum]"]
  R12 = Resistor [tolerance=±5% resistance=100 package="0402 [SMD]"]
  R13 = Resistor [tolerance=±5% resistance=300 package="0402 [SMD]"]
  C3 = Electrolytic Capacitor [capacitance=1µF package="0605 [SMD, electrolytic]"]
  C4 = Tantalum Capacitor [capacitance=0.1µF package="D 7343 [SMD, tantalum]"]
  lm318 = NPN-Transistor [package="TO92 [THT]"]
  Componente6 = BMP180 Breakout [part_number=SEN-11824]
  TSL_light = TSL2561 SparkFun Luminosity Sensor Breakout [part_number="SEN-12055 "]
  Componente7 = Gas Sensor Breakout Board
  Componente8 = Gas Sensor Breakout Board
  Componente9 = Gas Sensor Breakout Board  # not connected
  Componente10 = Gas Sensor Breakout Board  # not connected

nets:
  N1: Componente1.D21/SCL, Componente5.SCL, Componente6.SCL, TSL_light.SCL
  N2: Componente1.D20/SDA, Componente5.SDA, Componente6.SDA, TSL_light.SDA
  N3: Componente2.D8, Shinyei_PPD42.pin2
  N4: Componente2.PWM_D9, Shinyei_PPD42.pin4
  N5: Componente2.D7, RHT1.GND_1
  3.3V: RHT1.Vcc, R10.Pin_1, C2.+, Componente6.3.3V, TSL_light.3.3V
  GND: RHT1.GND_2, Componente6.GND, TSL_light.GND
  N6: Componente5.5V, R12.Pin_1, C3.+
  N7: Componente5.GND, Shinyei_PPD42.pin3, Shinyei_PPD42.pin5
  N8: lm317.E, U1.+, C1.+, C4.+, lm318.E
  N9: lm317.B, R10.Pin_0, R11.Pin_0
  N10: U1.-, R11.Pin_1, C2.-, C1.-, R13.Pin_1, C3.-, C4.-
  N11: R12.Pin_0, R13.Pin_0, lm318.B
  N12: Componente7.A1, Componente7.H1, Componente8.H1, Componente8.A1
  GND_2: Componente7.GND, Componente8.GND

notes:
  Salida de 3.3V
  Salida de 5V

custom parts:
  BMP180 Breakout: This is a breadboard friendly breakout board for the BMP180 high-precision, temp and pressure sensor.
  TSL2561 SparkFun Luminosity Sensor Breakout: The TSL2561 SparkFun Luminosity Sensor Breakout is a sophisticated light sensor which has a flat response across most of the visible spectrum. Unlike simpler sensors, the TSL2561 measures both infrared and visible light to better approximate the response of the human eye. And because the TSL2561 is an integrating sensor (it soaks up light for a predetermined amount of time), it is capable of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
